# Fritzing sketch mashControlMotor (saved by Fritzing 0.9.3b)
breadboards: 1

parts:
  Raspberry_Pi_1 = Raspberry Pi 3 [part_number=RPI-3-V1.2]
  J1 = double row male pin header, 6 pins [form="♂ (male)"]
  IC2 = L293D [package=THT]
  J2 = double row male pin header, 4 pins [form="♂ (male)"]

nets:
  N1: Raspberry_Pi_1.GPIO4, J1.pin2, IC2.In_1
  N2: Raspberry_Pi_1.GPIO17, J1.pin1, IC2.In_2
  N3: Raspberry_Pi_1.GPIO24, J1.pin3, IC2.In_3
  N4: Raspberry_Pi_1.GPIO23, J1.pin4, IC2.In_4
  N5: Raspberry_Pi_1.GND, J1.pin5, IC2.0V, J2.pin4
  N6: Raspberry_Pi_1.5V, J1.pin6, IC2.+Vmotor, IC2.+V
  N7: IC2.Enable_1, IC2.Enable_2
  N8: IC2.Out_2_(_Controlled_by_Enable_1_), J2.pin3
  N9: IC2.Out_3_(_Controlled_by_Enable_2_), J2.pin1
  N10: IC2.Out_4_(_Controlled_by_Enable_2_), J2.pin2
